// Digital circuit 5Estados.dig as structural Verilog
module _5Estados (
  input  Input,
  input  Clock,
  output UNLOCK
);

  wire and_1_out, and_2_out, and_3_out, and_4_out, and_5_out, not_1_out, not_2_out, not_3_out, or_1_out,
       or_2_out, Q_0_n, Q_1_n;

  not not_1 (not_1_out, Input);
  not not_2 (not_2_out, Q_1_n);
  not not_3 (not_3_out, Q_0_n);
  and and_1 (and_1_out, Input, Q_0_n, Q_1_n);
  and and_2 (and_2_out, Input, Q_0_n, not_2_out);
  and and_3 (and_3_out, not_3_out, Q_1_n);
  and and_4 (and_4_out, Input, not_3_out, not_2_out);
  and and_5 (and_5_out, not_1_out, not_3_out, Q_1_n);
  or or_1 (or_1_out, and_2_out, and_3_out);
  or or_2 (or_2_out, and_4_out, and_5_out);
  D_FF d_ff_1 (.D(and_1_out), .C(Clock), .Q(UNLOCK));  // open: nQ
  D_FF d_ff_2 (.D(or_1_out), .C(Clock), .Q(Q_1_n));  // open: nQ
  D_FF u_Q_0_n (.D(or_2_out), .C(Clock), .Q(Q_0_n));  // open: nQ

  // Other names for the same wires on the sheet: Q_2_n = UNLOCK

  // Notes on the sheet:
  //   Clock: Hz: 2
endmodule
